# Fritzing sketch Tildatiny (saved by Fritzing 0.7.10b)
breadboards: 1

parts:
  IC1 = H-Bridge [package=THT]
  M1 = DC Motor
  M2 = DC Motor
  VCC2 = Battery block 9V [part_number=9.6V]
  U1 = Voltage Regulator - 5V [package="TO220 [THT]"]
  D1 = Rectifier Diode [part_number=1N4001 package="300 mil [THT]"]
  C2 = Electrolytic Capacitor [capacitance=0.22mF voltage=16V package="100 mil [THT, electrolytic]"]
  C3 = Ceramic Capacitor [capacitance=100nF voltage=16V package="100 mil [THT, multilayer]"]
  R1 = Resistor [tolerance=±5% resistance=150 package=THT]
  R4 = Resistor [tolerance=±5% resistance=10k package=THT]
  R7 = Resistor [tolerance=±5% resistance=3.3k package=THT]
  LED2 = LED - 5mm [color="Green (560nm)" package="5 mm [THT]"]
  C5 = Ceramic Capacitor [capacitance=100nF voltage=6.3V part_number="WIMA 0.068" package="100 mil [THT, multilayer]"]
  Bauteil1 = IMU Digital Combo Board 6DOF
  RaspberryPi1 = Raspberry Pi Model B
  J1 = shrouded pin header, 6 pins [form="♂ (shrouded male)"]
  Q1 = NPN-Transistor [package="TO92 [THT]"]
  R8 = Resistor [tolerance=±5% resistance=12k package=THT]
  R9 = Resistor [tolerance=±5% resistance=12k package=THT]
  Q2 = NPN-Transistor [package="TO92 [THT]"]
  R10 = Resistor [tolerance=±5% resistance=3.9k package=THT]
  R11 = Resistor [tolerance=±5% resistance=3.9k package=THT]
  R12 = Resistor [tolerance=±5% resistance=1.5k package=THT]
  R13 = Resistor [tolerance=±5% resistance=1.5k package=THT]
  C4 = Ceramic Capacitor [capacitance=100nF voltage=16V package="100 mil [THT, multilayer]"]
  C6 = Electrolytic Capacitor [capacitance=1mF voltage=16V package="100 mil [THT, electrolytic]"]
  IC2 = IC, DIP package, 20 pins [chip_label=ATTiny861-20PU]
  R14 = Resistor [tolerance=±5% resistance=33k package=THT]
  R15 = Resistor [tolerance=±5% resistance=33k package=THT]
  R16 = Resistor [tolerance=±5% resistance=33k package=THT]
  R17 = Resistor [tolerance=±5% resistance=33k package=THT]
  R18 = Resistor [tolerance=±5% resistance=10k package=THT]
  R19 = Resistor [tolerance=±5% resistance=10k package=THT]
  R20 = Resistor [tolerance=±5% resistance=10k package=THT]
  R21 = Resistor [tolerance=±5% resistance=10k package=THT]
  R22 = Resistor [tolerance=±5% resistance=33k package=THT]
  J2 = Piezo Speaker
  LED1 = LED - 5mm [color="Red (633nm)" package="5 mm [THT]"]
  R23 = Resistor [tolerance=±5% resistance=30k package=THT]
  R24 = Resistor [tolerance=±5% resistance=10k package=THT]
  R25 = Resistor [tolerance=±5% resistance=10k package=THT]
  SONAR2 = Maxbotix MaxSonar Ultrasonic Sensor
  Bauteil2 = Triple Axis Magnetometer - HMC5883 Breakout

nets (from the breadboard view):
  N1: IC1.1A, Q2.C, R13.Pin_1
  N2: IC1.1Y, M2.pin_2, R17.Pin_1
  GND: IC1.GND2, IC1.GND3, VCC2.-, U1.GND, C2.-, C3.1, R1.Pin_0, R4.Pin_1, R7.Pin_1, C5.0, Bauteil1.GND, RaspberryPi1.GND, J1.pin4, Q1.E, R8.Pin_1, R9.Pin_0, Q2.E, C6.-, IC2.pin6, IC2.pin16, R18.Pin_1, R19.Pin_1, R20.Pin_1, R21.Pin_1, R24.Pin_0, R25.Pin_0, SONAR2.GND, Bauteil2.GND
  N3: IC1.2Y, M2.pin_1, R15.Pin_1
  N4: IC1.2A, R11.Pin_1, IC2.pin7
  N5: IC1.VCC2, VCC2.+, U1.input_voltage, D1.cathode, C2.+, C3.0, LED2.anode, R22.Pin_1
  N6: IC1.3_4EN, Q1.C, IC2.pin8, R25.Pin_1
  N7: IC1.3A, R12.Pin_0
  N8: IC1.3Y, M1.pin_2, R16.Pin_1
  N9: IC1.GND4, C4.1
  N10: IC1.4Y, M1.pin_1, R14.Pin_1
  N11: IC1.4A, R10.Pin_1, IC2.pin9
  5V: IC1.VCC1, U1.output_voltage, D1.anode, C5.1, RaspberryPi1.5V, R12.Pin_1, R13.Pin_0, C4.0, C6.+, IC2.pin5, IC2.pin15, R23.Pin_0, SONAR2.+5V
  N12: R1.Pin_1, J2.pin1
  N13: R4.Pin_0, IC2.pin14, R17.Pin_0
  3.3V: Bauteil1.3.3V, RaspberryPi1.3V3, Bauteil2.VCC
  N14: Bauteil1.SDA, RaspberryPi1.SDA, J1.pin5, IC2.pin1, Bauteil2.SDA
  N15: Bauteil1.SCL, RaspberryPi1.SCL, J1.pin2, IC2.pin3, Bauteil2.SCL
  N16: J1.pin1, IC2.pin2
  N17: J1.pin3, IC2.pin10, R23.Pin_1
  N18: Q1.B, R8.Pin_0, R10.Pin_0
  N19: R9.Pin_1, Q2.B, R11.Pin_0
  N20: IC2.pin4, R24.Pin_1
  N21: IC2.pin11, R14.Pin_0, R20.Pin_0
  N22: IC2.pin12, R16.Pin_0, R19.Pin_0
  N23: IC2.pin13, R15.Pin_0, R18.Pin_0
  N24: IC2.pin18, SONAR2.TX, SONAR2.RX
  N25: IC2.pin19, R21.Pin_0, R22.Pin_0
  N26: IC2.pin20, LED1.anode
  N27: J2.pin2, LED1.cathode

custom parts:
  Raspberry Pi Model B: Raspberry Pi (Model B)
  Maxbotix MaxSonar Ultrasonic Sensor: Maxbotix MaxSonar Ultrasonic Sensor LV-EZ0, LV-EZ1, LV-EZ2, LV-EZ3, LV-EZ4
